# Fritzing sketch Watering Station (saved by Fritzing 0.9.3b)
breadboards: 1

parts:
  Raspberry_Pi_1 = Raspberry Pi 3 [part_number=RPI-3-V1.2]
  U1 = 4-Channel 5v Relay Shield [package=relay-4ch5v10a]
  Part1 = Adafruit ADS1115 16Bit I2C ADC [part_number="Adafruit #1085"]
  M2 = DC Motor
  M3 = DC Motor
  M4 = DC Motor
  M1 = DC Motor
  부품3 = FC-28 Soil Hygrometer Module - Probe
  부품5 = FC-28 Soil Hygrometer Module
  부품6 = FC-28 Soil Hygrometer Module - Probe
  부품7 = FC-28 Soil Hygrometer Module - Probe
  부품8 = FC-28 Soil Hygrometer Module - Probe
  부품9 = FC-28 Soil Hygrometer Module
  부품10 = FC-28 Soil Hygrometer Module
  부품11 = FC-28 Soil Hygrometer Module

nets:
  3V3: Raspberry_Pi_1.3v3, Part1.VDD
  N1: Raspberry_Pi_1.GPIO2, Part1.SDA
  N2: Raspberry_Pi_1.GPIO3, Part1.SCL
  GND: Raspberry_Pi_1.GND, U1.GND, Part1.GND, 부품5.GND, 부품9.GND, 부품10.GND, 부품11.GND
  N3: Raspberry_Pi_1.GPIO17, U1.IN1
  N4: Raspberry_Pi_1.GPIO27, U1.IN2
  N5: Raspberry_Pi_1.GPIO22, U1.IN3
  N6: Raspberry_Pi_1.GPIO5, U1.IN4
  5V: Raspberry_Pi_1.5V, U1.VCC
  N7: U1.K1-On, M1.pin_2
  N8: U1.K2-On, M2.pin_2
  N9: U1.K3-On, M3.pin_2
  N10: U1.K4-On, M4.pin_2
  N11: Part1.AIN3, 부품11.AO
  N12: Part1.AIN2, 부품10.AO
  N13: Part1.AIN1, 부품9.AO
  N14: Part1.AIN0, 부품5.AO
  N15: 부품3.POS, 부품5.POS
  N16: 부품3.NEG, 부품5.NEG
  VCC: 부품5.VCC, 부품9.VCC, 부품10.VCC
  N17: 부품6.POS, 부품9.POS
  N18: 부품6.NEG, 부품9.NEG
  N19: 부품7.POS, 부품10.POS
  N20: 부품7.NEG, 부품10.NEG
  N21: 부품8.POS, 부품11.POS
  N22: 부품8.NEG, 부품11.NEG

custom parts:
  4-Channel 5v Relay Shield: 4 Channel 5v Relay Shield w. 2x SPD-06VDC-SD-C
  Adafruit ADS1115 16Bit I2C ADC: For microcontrollers without an analog-to-digital converter or when you want a higher-precision ADC, the ADS1115 provides 16-bit precision at 860 samples/second over I2C. The chip can be configured as 4 single-ended input channels, or two differential channels. As a nice bonus, it even includes a programmable gain amplifier, up to x16, to help boost up smaller single/differential signals to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
  FC-28 Soil Hygrometer Module - Probe: The FC-28 is a soil hygrometer module that uses the Texas Instruments LM393 comparator chip to provide an analog measurement of soil humidity.
  FC-28 Soil Hygrometer Module: The FC-28 is a soil hygrometer module that uses the Texas Instruments LM393 comparator chip to provide an analog measurement of soil humidity. The digital output is high when soil moisture is over a certain threshold, as determined by adjusting the potentiometer.
